// Logisim project control-logic.circ as structural Verilog: 1 circuit, main circuit control_logic
module control_logic (
  input  [31:0] Instruction,
  input  BrEq,
  input  BrLt,
  output PCSel,
  output RegWEn,
  output [2:0] ImmSel,
  output BrUn,
  output ASel,
  output BSel,
  output [3:0] ALUSel,
  output MemWEn,
  output [1:0] WBSel
);

  wire add, addi, and_1_out, and_2_out, and_3_out, and_4_out, and_5_out, and_6_out, and_r, andi, auipc,
       B_Type, beq, bge, bgeu, blt, bltu, bne, comparator_1_eq, comparator_2_eq, comparator_3_eq,
       comparator_4_eq, comparator_5_eq, comparator_6_eq, comparator_7_eq, comparator_8_eq, comparator_9_eq,
       comparator_10_eq, comparator_11_eq, comparator_13_eq, comparator_14_eq, comparator_15_eq,
       comparator_16_eq, comparator_17_eq, comparator_18_eq, comparator_19_eq, comparator_20_eq,
       comparator_21_eq, comparator_22_eq, comparator_23_eq, comparator_24_eq, comparator_25_eq,
       comparator_26_eq, comparator_27_eq, comparator_28_eq, comparator_29_eq, comparator_30_eq,
       comparator_31_eq, comparator_32_eq, comparator_33_eq, comparator_34_eq, comparator_35_eq,
       comparator_36_eq, comparator_38_eq, comparator_39_eq, comparator_40_eq, comparator_41_eq,
       comparator_42_eq, comparator_43_eq, comparator_46_eq, comparator_47_eq, comparator_48_eq,
       comparator_50_eq, comparator_51_eq, comparator_52_eq, comparator_55_eq, I_Type1, I_Type2, I_Type3,
       jal, jalr, lb, lh, lui, lw, mul, mulh, mulhu, not_1_out, not_2_out, not_3_out, or_1_out, or_2_out,
       or_3_out, or_4_out, or_r, ori, R_Type, S_Type, sb, sh, sll_r, slli, slt, slti, sra_r, srai, srl_r,
       srli, sub, sw, valid_1, valid_2, xor_r, xori;
  wire [1:0] priority_encoder_2_out;
  wire [4:0] priority_encoder_1_out;
  wire [5:0] adder_1_out, bit_extender_1_out, bit_extender_2_out, InstructionSel;
  wire [15:14] rom_1_data;

  or or_1 (or_1_out, BrEq, not_1_out);
  not not_1 (not_1_out, BrLt);
  or or_2 (or_2_out, BrEq, not_2_out);
  not not_2 (not_2_out, BrLt);
  not not_3 (not_3_out, BrEq);
  and and_1 (and_1_out, beq, BrEq);
  and and_2 (and_2_out, bge, or_1_out);
  and and_3 (and_3_out, bgeu, or_2_out);
  and and_4 (and_4_out, blt, BrLt);
  and and_5 (and_5_out, bltu, BrLt);
  and and_6 (and_6_out, bne, not_3_out);
  Comparator #(.width(3)) comparator_1 (.a(3'b000), .b(Instruction[14:12]), .eq(comparator_1_eq));  // open: gt, lt
  Comparator #(.width(3)) comparator_2 (.a(3'b111), .b(Instruction[14:12]), .eq(comparator_2_eq));  // open: gt, lt
  Comparator #(.width(3)) comparator_3 (.a(3'b110), .b(Instruction[14:12]), .eq(comparator_3_eq));  // open: gt, lt
  Comparator #(.width(3)) comparator_4 (.a(3'b100), .b(Instruction[14:12]), .eq(comparator_4_eq));  // open: gt, lt
  Comparator #(.width(3)) comparator_5 (.a(3'b001), .b(Instruction[14:12]), .eq(comparator_5_eq));  // open: gt, lt
  Comparator #(.width(7)) comparator_6 (.a(Instruction[31:25]), .b({7{1'b0}}), .eq(comparator_6_eq));  // open: gt, lt
  Comparator #(.width(3)) comparator_7 (.a(3'b101), .b(Instruction[14:12]), .eq(comparator_7_eq));  // open: gt, lt
  Comparator #(.width(7)) comparator_8 (.a(Instruction[31:25]), .b({7{1'b0}}), .eq(comparator_8_eq));  // open: gt, lt
  Comparator #(.width(3)) comparator_9 (.a(3'b101), .b(Instruction[14:12]), .eq(comparator_9_eq));  // open: gt, lt
  Comparator #(.width(7)) comparator_10 (
    .a(Instruction[31:25]), .b(7'b0100000), .eq(comparator_10_eq));  // open: gt, lt
  Comparator #(.width(3)) comparator_11 (.a(3'b010), .b(Instruction[14:12]), .eq(comparator_11_eq));  // open: gt, lt
  Comparator #(.width(7)) comparator_12 (.a(7'b0010011), .b(Instruction[6:0]), .eq(I_Type1));  // open: gt, lt
  and and_7 (addi, I_Type1, comparator_1_eq);
  and and_8 (andi, I_Type1, comparator_2_eq);
  and and_9 (ori, I_Type1, comparator_3_eq);
  and and_10 (xori, I_Type1, comparator_4_eq);
  and and_11 (slti, I_Type1, comparator_11_eq);
  and and_12 (slli, I_Type1, comparator_5_eq, comparator_6_eq);
  and and_13 (srli, I_Type1, comparator_7_eq, comparator_8_eq);
  and and_14 (srai, I_Type1, comparator_9_eq, comparator_10_eq);
  ROM #(.addrWidth(6), .dataWidth(16)) rom_1 (
    .addr(InstructionSel), .data({rom_1_data, WBSel, MemWEn, ALUSel, BSel, ASel, BrUn, ImmSel, RegWEn}));
  or or_3 (or_3_out, and_1_out, and_2_out, and_3_out, and_4_out, and_5_out, and_6_out);
  or or_4 (or_4_out, jal, jalr);
  or or_5 (PCSel, or_3_out, or_4_out);
  Comparator #(.width(3)) comparator_13 (.a(3'b000), .b(Instruction[14:12]), .eq(comparator_13_eq));  // open: gt, lt
  Comparator #(.width(7)) comparator_14 (.a(Instruction[31:25]), .b({7{1'b0}}), .eq(comparator_14_eq));  // open: gt, lt
  Comparator #(.width(3)) comparator_15 (.a(3'b000), .b(Instruction[14:12]), .eq(comparator_15_eq));  // open: gt, lt
  Comparator #(.width(7)) comparator_16 (
    .a(Instruction[31:25]), .b(7'b0100000), .eq(comparator_16_eq));  // open: gt, lt
  Comparator #(.width(3)) comparator_17 (.a(3'b111), .b(Instruction[14:12]), .eq(comparator_17_eq));  // open: gt, lt
  Comparator #(.width(7)) comparator_18 (.a(Instruction[31:25]), .b({7{1'b0}}), .eq(comparator_18_eq));  // open: gt, lt
  Comparator #(.width(3)) comparator_19 (.a(3'b110), .b(Instruction[14:12]), .eq(comparator_19_eq));  // open: gt, lt
  Comparator #(.width(7)) comparator_20 (.a(Instruction[31:25]), .b({7{1'b0}}), .eq(comparator_20_eq));  // open: gt, lt
  Comparator #(.width(3)) comparator_21 (.a(3'b100), .b(Instruction[14:12]), .eq(comparator_21_eq));  // open: gt, lt
  Comparator #(.width(7)) comparator_22 (.a(Instruction[31:25]), .b({7{1'b0}}), .eq(comparator_22_eq));  // open: gt, lt
  Comparator #(.width(3)) comparator_23 (.a(3'b001), .b(Instruction[14:12]), .eq(comparator_23_eq));  // open: gt, lt
  Comparator #(.width(7)) comparator_24 (.a(Instruction[31:25]), .b({7{1'b0}}), .eq(comparator_24_eq));  // open: gt, lt
  Comparator #(.width(3)) comparator_25 (.a(3'b101), .b(Instruction[14:12]), .eq(comparator_25_eq));  // open: gt, lt
  Comparator #(.width(7)) comparator_26 (.a(Instruction[31:25]), .b({7{1'b0}}), .eq(comparator_26_eq));  // open: gt, lt
  Comparator #(.width(3)) comparator_27 (.a(3'b101), .b(Instruction[14:12]), .eq(comparator_27_eq));  // open: gt, lt
  Comparator #(.width(7)) comparator_28 (
    .a(Instruction[31:25]), .b(7'b0100000), .eq(comparator_28_eq));  // open: gt, lt
  Comparator #(.width(3)) comparator_29 (.a(3'b010), .b(Instruction[14:12]), .eq(comparator_29_eq));  // open: gt, lt
  Comparator #(.width(7)) comparator_30 (.a(Instruction[31:25]), .b({7{1'b0}}), .eq(comparator_30_eq));  // open: gt, lt
  Comparator #(.width(3)) comparator_31 (.a(3'b000), .b(Instruction[14:12]), .eq(comparator_31_eq));  // open: gt, lt
  Comparator #(.width(7)) comparator_32 (
    .a(Instruction[31:25]), .b(7'b0000001), .eq(comparator_32_eq));  // open: gt, lt
  Comparator #(.width(3)) comparator_33 (.a(3'b001), .b(Instruction[14:12]), .eq(comparator_33_eq));  // open: gt, lt
  Comparator #(.width(7)) comparator_34 (
    .a(Instruction[31:25]), .b(7'b0000001), .eq(comparator_34_eq));  // open: gt, lt
  Comparator #(.width(3)) comparator_35 (.a(3'b011), .b(Instruction[14:12]), .eq(comparator_35_eq));  // open: gt, lt
  Comparator #(.width(7)) comparator_36 (
    .a(Instruction[31:25]), .b(7'b0000001), .eq(comparator_36_eq));  // open: gt, lt
  Comparator #(.width(7)) comparator_37 (.a(7'b0110011), .b(Instruction[6:0]), .eq(R_Type));  // open: gt, lt
  and and_15 (add, R_Type, comparator_13_eq, comparator_14_eq);
  and and_16 (sub, R_Type, comparator_15_eq, comparator_16_eq);
  and and_17 (and_r, R_Type, comparator_17_eq, comparator_18_eq);
  and and_18 (or_r, R_Type, comparator_19_eq, comparator_20_eq);
  and and_19 (xor_r, R_Type, comparator_21_eq, comparator_22_eq);
  and and_20 (sll_r, R_Type, comparator_23_eq, comparator_24_eq);
  and and_21 (srl_r, R_Type, comparator_25_eq, comparator_26_eq);
  and and_22 (sra_r, R_Type, comparator_27_eq, comparator_28_eq);
  and and_23 (slt, R_Type, comparator_29_eq, comparator_30_eq);
  and and_24 (mul, R_Type, comparator_31_eq, comparator_32_eq);
  and and_25 (mulh, R_Type, comparator_33_eq, comparator_34_eq);
  and and_26 (mulhu, R_Type, comparator_35_eq, comparator_36_eq);
  Comparator #(.width(3)) comparator_38 (.a(3'b000), .b(Instruction[14:12]), .eq(comparator_38_eq));  // open: gt, lt
  Comparator #(.width(3)) comparator_39 (.a(3'b101), .b(Instruction[14:12]), .eq(comparator_39_eq));  // open: gt, lt
  Comparator #(.width(3)) comparator_40 (.a(3'b111), .b(Instruction[14:12]), .eq(comparator_40_eq));  // open: gt, lt
  Comparator #(.width(3)) comparator_41 (.a(3'b100), .b(Instruction[14:12]), .eq(comparator_41_eq));  // open: gt, lt
  Comparator #(.width(3)) comparator_42 (.a(3'b110), .b(Instruction[14:12]), .eq(comparator_42_eq));  // open: gt, lt
  Comparator #(.width(3)) comparator_43 (.a(3'b001), .b(Instruction[14:12]), .eq(comparator_43_eq));  // open: gt, lt
  Comparator #(.width(7)) comparator_44 (.a(7'b1100011), .b(Instruction[6:0]), .eq(B_Type));  // open: gt, lt
  and and_27 (beq, B_Type, comparator_38_eq);
  and and_28 (bge, B_Type, comparator_39_eq);
  and and_29 (bgeu, B_Type, comparator_40_eq);
  and and_30 (blt, B_Type, comparator_41_eq);
  and and_31 (bltu, B_Type, comparator_42_eq);
  and and_32 (bne, B_Type, comparator_43_eq);
  Priority_Encoder #(.select(5)) priority_encoder_1 (
    .in0(add), .in1(mul), .in2(sub), .in3(sll_r), .in4(mulh), .in5(mulhu), .in6(slt), .in7(xor_r),
    .in8(srl_r), .in9(sra_r), .in10(or_r), .in11(and_r), .in12(lb), .in13(lh), .in14(lw), .in15(addi),
    .in16(slli), .in17(slti), .in18(xori), .in19(srli), .in20(srai), .in21(ori), .in22(andi), .in23(sb),
    .in24(sh), .in25(sw), .in26(beq), .in27(bne), .in28(blt), .in29(bge), .in30(bltu), .in31(bgeu),
    .out(priority_encoder_1_out), .gs(valid_1));  // open: en_out, en_in
  Priority_Encoder #(.select(2)) priority_encoder_2 (
    .in0(auipc), .in1(lui), .in2(jal), .in3(jalr), .out(priority_encoder_2_out), .gs(valid_2));  // open: en_out, en_in
  assign bit_extender_1_out = {{1{1'b0}}, priority_encoder_1_out};  // Bit_Extender bit_extender_1
  assign bit_extender_2_out = {{4{1'b0}}, priority_encoder_2_out};  // Bit_Extender bit_extender_2
  Comparator #(.width(7)) comparator_45 (.a(7'b0000011), .b(Instruction[6:0]), .eq(I_Type2));  // open: gt, lt
  Comparator #(.width(3)) comparator_46 (.a(3'b000), .b(Instruction[14:12]), .eq(comparator_46_eq));  // open: gt, lt
  Comparator #(.width(3)) comparator_47 (.a(3'b001), .b(Instruction[14:12]), .eq(comparator_47_eq));  // open: gt, lt
  Comparator #(.width(3)) comparator_48 (.a(3'b010), .b(Instruction[14:12]), .eq(comparator_48_eq));  // open: gt, lt
  Adder #(.width(6)) adder_1 (.a(6'b100000), .b(bit_extender_2_out), .out(adder_1_out));  // open: cin, cout
  and and_33 (lb, I_Type2, comparator_46_eq);
  and and_34 (lh, I_Type2, comparator_47_eq);
  and and_35 (lw, I_Type2, comparator_48_eq);
  Multiplexer #(.enable("false"), .width(6)) multiplexer_1 (
    .in0(bit_extender_1_out), .in1(adder_1_out), .out(InstructionSel), .sel(valid_2));
  Comparator #(.width(7)) comparator_49 (.a(7'b0100011), .b(Instruction[6:0]), .eq(S_Type));  // open: gt, lt
  Comparator #(.width(3)) comparator_50 (.a(3'b000), .b(Instruction[14:12]), .eq(comparator_50_eq));  // open: gt, lt
  Comparator #(.width(3)) comparator_51 (.a(3'b001), .b(Instruction[14:12]), .eq(comparator_51_eq));  // open: gt, lt
  Comparator #(.width(3)) comparator_52 (.a(3'b010), .b(Instruction[14:12]), .eq(comparator_52_eq));  // open: gt, lt
  and and_36 (sb, S_Type, comparator_50_eq);
  and and_37 (sh, S_Type, comparator_51_eq);
  and and_38 (sw, S_Type, comparator_52_eq);
  Comparator #(.width(7)) comparator_53 (.a(7'b1101111), .b(Instruction[6:0]), .eq(jal));  // open: gt, lt
  Comparator #(.width(7)) comparator_54 (.a(7'b1100111), .b(Instruction[6:0]), .eq(I_Type3));  // open: gt, lt
  Comparator #(.width(3)) comparator_55 (.a(3'b000), .b(Instruction[14:12]), .eq(comparator_55_eq));  // open: gt, lt
  and and_39 (jalr, I_Type3, comparator_55_eq);
  Comparator #(.width(7)) comparator_56 (.a(7'b0010111), .b(Instruction[6:0]), .eq(auipc));  // open: gt, lt
  Comparator #(.width(7)) comparator_57 (.a(7'b0110111), .b(Instruction[6:0]), .eq(lui));  // open: gt, lt

  // Other names for the same wires on the sheet: opcode[6:0] = Instruction[6:0]; func3[2:0] = Instruction[14:12];
  //   func7[6:0] = Instruction[31:25]

  // Notes on the sheet:
  //   INPUTS to your circuit
  //   DON'T CHANGE THE LOCATIONS OF THE INPUTS AND OUTPUTS!
  //   contents of rom_1 (hex, n*v repeats v):
  //   1001 1401 1601 1081 1481 1581 1101 1201 1281 1681 1301 1381 41 41 41 1041 10c1 1141 1241 12c1 16c1
  //   1341 13c1 1843 1843 1843 4*64 74 74 1067 17e7 2069 2041
  //   OUTPUT from your circuit
  //   ROM FOR CONTROL LOGIC
  //   This is only if you choose to do the ROM option
  //   CONNECT
  //   WIRE
  //   TO
  //   USE
  //   ROM
endmodule
