// Logisim project partial-load.circ as structural Verilog: 1 circuit, main circuit partial_load
module partial_load (
  input  [31:0] Instruction,
  input  [31:0] MemAddress,
  input  [31:0] DataFromMem,
  output [31:0] DataToReg
);

  wire [7:0] multiplexer_2_out;
  wire [15:0] multiplexer_3_out;
  wire [31:0] lb_out, lh_out;

  Multiplexer #(.enable("false"), .select(3), .width(32)) multiplexer_1 (
    .in0(lb_out), .in1(lh_out), .in2(DataFromMem), .out(DataToReg), .sel(Instruction[14:12]));  // open: in3, in4, in5, in6, in7
  Multiplexer #(.enable("false"), .select(2), .width(8)) multiplexer_2 (
    .in0(DataFromMem[7:0]), .in1(DataFromMem[15:8]), .in2(DataFromMem[23:16]), .in3(DataFromMem[31:24]),
    .out(multiplexer_2_out), .sel(MemAddress[1:0]));
  Multiplexer #(.enable("false"), .select(2), .width(16)) multiplexer_3 (
    .in0(DataFromMem[15:0]), .in1(DataFromMem[23:8]), .in2(DataFromMem[31:16]), .out(multiplexer_3_out),
    .sel(MemAddress[1:0]));  // open: in3
  assign lb_out = {{24{multiplexer_2_out[7]}}, multiplexer_2_out};  // Bit_Extender bit_extender_1
  assign lh_out = {{16{multiplexer_3_out[15]}}, multiplexer_3_out};  // Bit_Extender bit_extender_2

  // Other names for the same wires on the sheet: func3[2:0] = Instruction[14:12]; byte0[7:0] = DataFromMem[7:0];
  //   half0[15:0] = DataFromMem[15:0]; lw_out[31:0] = DataFromMem; byte1[7:0] = DataFromMem[15:8];
  //   half1[15:0] = DataFromMem[23:8]; byte2[7:0] = DataFromMem[23:16]; half2[15:0] = DataFromMem[31:16];
  //   byte3[7:0] = DataFromMem[31:24]; bottom[1:0] = MemAddress[1:0]

  // Notes on the sheet:
  //   INPUTS to your circuit
  //   DON'T CHANGE THE LOCATIONS OF THE INPUTS AND OUTPUTS!
  //   OUTPUT from your circuit
endmodule
