// Logisim project partial-store.circ as structural Verilog: 1 circuit, main circuit partial_store
module partial_store (
  input  [31:0] Instruction,
  input  [31:0] MemAddress,
  input  [31:0] DataFromReg,
  input  MemWEn,
  output [3:0] MemWriteMask,
  output [31:0] DataToMem
);

  wire [3:0] mask, mask1, mask2;
  wire [31:0] sb_out, sh_out;

  Multiplexer #(.enable("false"), .select(2), .width(4)) multiplexer_1 (
    .in0(4'b0001), .in1(4'b0010), .in2(4'b0100), .in3(4'b1000), .out(mask1), .sel(MemAddress[1:0]));
  Multiplexer #(.enable("false"), .select(3), .width(4)) multiplexer_2 (
    .in0(mask1), .in1(mask2), .in2(4'b1111), .out(mask), .sel(Instruction[14:12]));  // open: in3, in4, in5, in6, in7
  Multiplexer #(.enable("false"), .select(3), .width(32)) multiplexer_3 (
    .in0(sb_out), .in1(sh_out), .in2(DataFromReg), .out(DataToMem), .sel(Instruction[14:12]));  // open: in3, in4, in5, in6, in7
  Multiplexer #(.enable("false"), .select(2), .width(4)) multiplexer_4 (
    .in0(4'b0011), .in2(4'b1100), .out(mask2), .sel(MemAddress[1:0]));  // open: in1, in3
  Multiplexer #(.enable("false"), .width(4)) multiplexer_5 (
    .in0(4'b0000), .in1(mask), .out(MemWriteMask), .sel(MemWEn));
  Multiplexer #(.enable("false"), .select(2), .width(32)) multiplexer_6 (
    .in0({{16{1'b0}}, DataFromReg[15:0]}), .in2({DataFromReg[15:0], {16{1'b0}}}), .out(sh_out),
    .sel(MemAddress[1:0]));  // open: in1, in3
  Multiplexer #(.enable("false"), .select(2), .width(32)) multiplexer_7 (
    .in0({{24{1'b0}}, DataFromReg[7:0]}), .in1({{16{1'b0}}, DataFromReg[7:0], {8{1'b0}}}),
    .in2({{8{1'b0}}, DataFromReg[7:0], {16{1'b0}}}), .in3({DataFromReg[7:0], {24{1'b0}}}), .out(sb_out),
    .sel(MemAddress[1:0]));

  // Other names for the same wires on the sheet: byte[7:0] = DataFromReg[7:0]; half[15:0] = DataFromReg[15:0];
  //   sw_out[31:0] = DataFromReg; func3[2:0] = Instruction[14:12]; bottom[1:0] = MemAddress[1:0]

  // Notes on the sheet:
  //   INPUTS to your circuit
  //   DON'T CHANGE THE LOCATIONS OF THE INPUTS AND OUTPUTS!
  //   OUTPUT from your circuit
endmodule
