// Logisim project regfile.circ as structural Verilog: 1 circuit, main circuit regfile
module regfile (
  input  [4:0] ReadReg1,
  input  [4:0] ReadReg2,
  input  [4:0] WriteReg,
  input  [31:0] RegWriteData,
  input  RegWEn,
  input  clk,
  output [31:0] ra,
  output [31:0] sp,
  output [31:0] t0,
  output [31:0] t1,
  output [31:0] t2,
  output [31:0] s0,
  output [31:0] s1,
  output [31:0] a0,
  output [31:0] RegReadData1,
  output [31:0] RegReadData2
);

  wire x1Enable, x2Enable, x3Enable, x4Enable, x5Enable, x6Enable, x7Enable, x8Enable, x9Enable, x10Enable,
       x11Enable, x12Enable, x13Enable, x14Enable, x15Enable, x16Enable, x17Enable, x18Enable, x19Enable,
       x20Enable, x21Enable, x22Enable, x23Enable, x24Enable, x25Enable, x26Enable, x27Enable, x28Enable,
       x29Enable, x30Enable, x31Enable;
  wire [31:0] x0, x3, x4, x11, x12, x13, x14, x15, x16, x17, x18, x19, x20, x21, x22, x23, x24, x25, x26,
       x27, x28, x29, x30, x31;

  Decoder #(.select(5)) decoder_1 (
    .out1(x1Enable), .out2(x2Enable), .out3(x3Enable), .out4(x4Enable), .out5(x5Enable), .out6(x6Enable),
    .out7(x7Enable), .out8(x8Enable), .out9(x9Enable), .out10(x10Enable), .out11(x11Enable),
    .out12(x12Enable), .out13(x13Enable), .out14(x14Enable), .out15(x15Enable), .out16(x16Enable),
    .out17(x17Enable), .out18(x18Enable), .out19(x19Enable), .out20(x20Enable), .out21(x21Enable),
    .out22(x22Enable), .out23(x23Enable), .out24(x24Enable), .out25(x25Enable), .out26(x26Enable),
    .out27(x27Enable), .out28(x28Enable), .out29(x29Enable), .out30(x30Enable), .out31(x31Enable),
    .sel(WriteReg), .en(RegWEn));  // open: out0
  Register #(.width(32)) register_1 (.D({32{1'b0}}), .en(1'b0), .clk(clk), .Q(x0));  // open: clr
  Register #(.width(32)) register_2 (.D(RegWriteData), .en(x1Enable), .clk(clk), .Q(ra));  // open: clr
  Register #(.width(32)) register_3 (.D(RegWriteData), .en(x2Enable), .clk(clk), .Q(sp));  // open: clr
  Register #(.width(32)) register_4 (.D(RegWriteData), .en(x3Enable), .clk(clk), .Q(x3));  // open: clr
  Register #(.width(32)) register_5 (.D(RegWriteData), .en(x4Enable), .clk(clk), .Q(x4));  // open: clr
  Register #(.width(32)) register_6 (.D(RegWriteData), .en(x5Enable), .clk(clk), .Q(t0));  // open: clr
  Register #(.width(32)) register_7 (.D(RegWriteData), .en(x6Enable), .clk(clk), .Q(t1));  // open: clr
  Register #(.width(32)) register_8 (.D(RegWriteData), .en(x7Enable), .clk(clk), .Q(t2));  // open: clr
  Register #(.width(32)) register_9 (.D(RegWriteData), .en(x8Enable), .clk(clk), .Q(s0));  // open: clr
  Register #(.width(32)) register_10 (.D(RegWriteData), .en(x9Enable), .clk(clk), .Q(s1));  // open: clr
  Register #(.width(32)) register_11 (.D(RegWriteData), .en(x10Enable), .clk(clk), .Q(a0));  // open: clr
  Register #(.width(32)) register_12 (.D(RegWriteData), .en(x11Enable), .clk(clk), .Q(x11));  // open: clr
  Register #(.width(32)) register_13 (.D(RegWriteData), .en(x12Enable), .clk(clk), .Q(x12));  // open: clr
  Register #(.width(32)) register_14 (.D(RegWriteData), .en(x13Enable), .clk(clk), .Q(x13));  // open: clr
  Register #(.width(32)) register_15 (.D(RegWriteData), .en(x14Enable), .clk(clk), .Q(x14));  // open: clr
  Register #(.width(32)) register_16 (.D(RegWriteData), .en(x15Enable), .clk(clk), .Q(x15));  // open: clr
  Register #(.width(32)) register_17 (.D(RegWriteData), .en(x16Enable), .clk(clk), .Q(x16));  // open: clr
  Register #(.width(32)) register_18 (.D(RegWriteData), .en(x17Enable), .clk(clk), .Q(x17));  // open: clr
  Register #(.width(32)) register_19 (.D(RegWriteData), .en(x18Enable), .clk(clk), .Q(x18));  // open: clr
  Register #(.width(32)) register_20 (.D(RegWriteData), .en(x19Enable), .clk(clk), .Q(x19));  // open: clr
  Register #(.width(32)) register_21 (.D(RegWriteData), .en(x20Enable), .clk(clk), .Q(x20));  // open: clr
  Register #(.width(32)) register_22 (.D(RegWriteData), .en(x21Enable), .clk(clk), .Q(x21));  // open: clr
  Register #(.width(32)) register_23 (.D(RegWriteData), .en(x22Enable), .clk(clk), .Q(x22));  // open: clr
  Register #(.width(32)) register_24 (.D(RegWriteData), .en(x23Enable), .clk(clk), .Q(x23));  // open: clr
  Register #(.width(32)) register_25 (.D(RegWriteData), .en(x24Enable), .clk(clk), .Q(x24));  // open: clr
  Register #(.width(32)) register_26 (.D(RegWriteData), .en(x25Enable), .clk(clk), .Q(x25));  // open: clr
  Register #(.width(32)) register_27 (.D(RegWriteData), .en(x26Enable), .clk(clk), .Q(x26));  // open: clr
  Register #(.width(32)) register_28 (.D(RegWriteData), .en(x27Enable), .clk(clk), .Q(x27));  // open: clr
  Register #(.width(32)) register_29 (.D(RegWriteData), .en(x28Enable), .clk(clk), .Q(x28));  // open: clr
  Register #(.width(32)) register_30 (.D(RegWriteData), .en(x29Enable), .clk(clk), .Q(x29));  // open: clr
  Register #(.width(32)) register_31 (.D(RegWriteData), .en(x30Enable), .clk(clk), .Q(x30));  // open: clr
  Register #(.width(32)) register_32 (.D(RegWriteData), .en(x31Enable), .clk(clk), .Q(x31));  // open: clr
  Multiplexer #(.enable("false"), .select(5), .width(32)) multiplexer_1 (
    .in0(x0), .in1(ra), .in2(sp), .in3(x3), .in4(x4), .in5(t0), .in6(t1), .in7(t2), .in8(s0), .in9(s1),
    .in10(a0), .in11(x11), .in12(x12), .in13(x13), .in14(x14), .in15(x15), .in16(x16), .in17(x17),
    .in18(x18), .in19(x19), .in20(x20), .in21(x21), .in22(x22), .in23(x23), .in24(x24), .in25(x25),
    .in26(x26), .in27(x27), .in28(x28), .in29(x29), .in30(x30), .in31(x31), .out(RegReadData1), .sel(ReadReg1));
  Multiplexer #(.enable("false"), .select(5), .width(32)) multiplexer_2 (
    .in0(x0), .in1(ra), .in2(sp), .in3(x3), .in4(x4), .in5(t0), .in6(t1), .in7(t2), .in8(s0), .in9(s1),
    .in10(a0), .in11(x11), .in12(x12), .in13(x13), .in14(x14), .in15(x15), .in16(x16), .in17(x17),
    .in18(x18), .in19(x19), .in20(x20), .in21(x21), .in22(x22), .in23(x23), .in24(x24), .in25(x25),
    .in26(x26), .in27(x27), .in28(x28), .in29(x29), .in30(x30), .in31(x31), .out(RegReadData2), .sel(ReadReg2));

  // Other names for the same wires on the sheet: x1[31:0] = ra; x2[31:0] = sp; x5[31:0] = t0; x6[31:0] = t1;
  //   x7[31:0] = t2; x8[31:0] = s0; x9[31:0] = s1; x10[31:0] = a0

  // Notes on the sheet:
  //   INPUTS to your circuit
  //   DON'T CHANGE THE LOCATIONS OF THE INPUTS AND OUTPUTS!
  //   These are DEBUG/TEST outputs from your circuit.
  //   OUTPUTS from your circuit
endmodule
